// Logisim project Claw Machine.circ as structural Verilog: 1 circuit, main circuit main
module main (
  input  [2:0] Up,
  input  [2:0] Right,
  input  [2:0] Down,
  input  [2:0] Left
);

  wire and_1_out, and_2_out, and_3_out, and_4_out, and_5_out, and_6_out, and_7_out, and_8_out, button_2_out,
       button_3_out, button_out, clock_1_out, decoder_1_out0, decoder_1_out1, decoder_1_out2, decoder_1_out3,
       not_1_out, not_2_out, not_3_out, not_4_out, not_5_out, or_1_out, or_2_out, v_out;
  wire [1:0] A1_q;
  wire [2:0] controlled_buffer_1_out;

  assign controlled_buffer_1_out = button_2_out ? Up : 3'bz;  // Controlled_Buffer controlled_buffer_1
  assign controlled_buffer_1_out = button_3_out ? Right : 3'bz;  // Controlled_Buffer controlled_buffer_2
  assign controlled_buffer_1_out = v_out ? Down : 3'bz;  // Controlled_Buffer controlled_buffer_3
  assign controlled_buffer_1_out = button_out ? Left : 3'bz;  // Controlled_Buffer controlled_buffer_4
  not not_1 (not_1_out, controlled_buffer_1_out[2]);
  not not_2 (not_2_out, controlled_buffer_1_out[1]);
  LED led_1 (.in(decoder_1_out3));
  LED led_2 (.in(decoder_1_out0));
  Button button (.out(button_out));
  Button v (.out(v_out));
  not not_3 (not_3_out, controlled_buffer_1_out[0]);
  LED led_3 (.in(decoder_1_out1));
  LED led_4 (.in(decoder_1_out2));
  Button button_2 (.out(button_2_out));
  Button button_3 (.out(button_3_out));
  Decoder #(.select(2), .enable("false")) decoder_1 (
    .out0(decoder_1_out0), .out1(decoder_1_out1), .out2(decoder_1_out2), .out3(decoder_1_out3), .sel(A1_q));
  and and_1 (and_1_out, not_1_out, not_2_out, not_3_out);
  and and_2 (and_2_out, not_1_out, controlled_buffer_1_out[0], A1_q[0]);
  and and_3 (and_3_out, A1_q[0], not_1_out, not_2_out, not_3_out, A1_q[1]);
  and and_4 (and_4_out, not_4_out, not_1_out, controlled_buffer_1_out[1], not_3_out, A1_q[1]);
  and and_5 (and_5_out, not_4_out, not_1_out, not_2_out, not_5_out);
  and and_6 (and_6_out, not_4_out, not_1_out, not_2_out, controlled_buffer_1_out[0]);
  and and_7 (and_7_out, A1_q[0], not_1_out, controlled_buffer_1_out[1], not_5_out);
  and and_8 (and_8_out, A1_q[0], not_1_out, controlled_buffer_1_out[1], controlled_buffer_1_out[0]);
  not not_4 (not_4_out, A1_q[0]);
  or or_1 (or_1_out, and_1_out, and_2_out);
  not not_5 (not_5_out, A1_q[1]);
  or or_2 (or_2_out, and_3_out, and_4_out, and_5_out, and_6_out, and_7_out, and_8_out);
  Clock clock_1 (.out(clock_1_out));
  D_Flip_Flop A1 (.clk(clock_1_out), .D(or_1_out), .Q(A1_q[0]));  // open: Qn, preset, en, reset
  D_Flip_Flop A2 (.clk(clock_1_out), .D(or_2_out), .Q(A1_q[1]));  // open: Qn, preset, en, reset
endmodule
